// Logisim project lab7.circ as structural Verilog: 7 circuits, main circuit main
module main (
  input  in_1,
  input  in_2,
  input  in_3,
  input  in_4,
  input  in_5,
  input  in_6,
  output out_7,
  output out_8,
  output out_9,
  output [7:0] out_10,
  output [7:0] out_11
);

  AddMachine addmachine_1 (.out_1(out_10), .out_2(out_11));
  NAND nand_1 (.Input_1(in_1), .Input_2(in_2), .Output(out_7));
  NOR nor_1 (.Input_1(in_3), .IInput_2(in_3), .Output(out_8));
  XOR xor_1 (.Input_1(in_5), .Input_2(in_6), .Output(out_9));

  assign in_4 = in_3;
endmodule

module NAND (
  input  Input_1,
  input  Input_2,
  output Output
);

  wire not_1_out, not_2_out;

  not not_1 (not_1_out, Input_1);
  not not_2 (not_2_out, Input_2);
  or or_1 (Output, not_1_out, not_2_out);
endmodule

module NOR (
  input  Input_1,
  input  IInput_2,
  output Output
);

  wire not_1_out, not_2_out;

  not not_1 (not_1_out, Input_1);
  not not_2 (not_2_out, IInput_2);
  and and_1 (Output, not_1_out, not_2_out);
endmodule

module XOR (
  input  Input_1,
  input  Input_2,
  output Output
);

  wire not_1_out, not_2_out, or_1_out, or_2_out;

  not not_1 (not_1_out, Input_1);
  not not_2 (not_2_out, Input_2);
  or or_1 (or_1_out, Input_1, Input_2);
  or or_2 (or_2_out, not_1_out, not_2_out);
  and and_1 (Output, or_1_out, or_2_out);
endmodule

module _2_to_1_MUX (
  input  Input_1,
  input  Selector,
  input  Input_2,
  output Output
);

  wire and_1_out, and_2_out, not_1_out;

  and and_1 (and_1_out, Input_1, Selector);
  not not_1 (not_1_out, Selector);
  and and_2 (and_2_out, not_1_out, Input_2);
  or or_1 (Output, and_1_out, and_2_out);
endmodule

module _4_to_1_MUX (
  input  Selector_1,
  input  Selector_0,
  input  Input_1,
  input  Input_2,
  input  Input_3,
  input  Input_4,
  output Output
);

  wire and_1_out, and_2_out, and_3_out, and_4_out, not_1_out, not_2_out;

  not not_1 (not_1_out, Selector_0);
  not not_2 (not_2_out, Selector_1);
  and and_1 (and_1_out, Input_1, not_2_out, not_1_out);
  and and_2 (and_2_out, Input_2, Selector_1, not_1_out);
  and and_3 (and_3_out, Input_3, not_2_out, Selector_0);
  and and_4 (and_4_out, Input_4, Selector_1, Selector_0);
  or or_1 (Output, and_1_out, and_2_out, and_3_out, and_4_out);
endmodule

module AddMachine (
  output [7:0] out_1,
  output [7:0] out_2
);

  wire clock_1_out;

  Adder adder_1 (.a(8'h1), .b(out_2), .out(out_1));  // open: cin, cout
  Clock clock_1 (.out(clock_1_out));
  Register register_1 (.D(out_1), .Q(out_2), .clk(clock_1_out));  // open: en, clr
endmodule
