// Logisim project lab9.circ as structural Verilog
module Ex1 (
  input  [7:0] Input,
  output Out_1,
  output [7:0] Out_2
);

  and and_1 (Out_1, Input[0], Input[7]);
  not not_1 (Out_2[7], Input[7]);

  assign Out_2[6:0] = Input[6:0];
endmodule

module rotr (
  input  [15:0] in_1,
  input  [3:0] in_2,
  output [15:0] out_3
);

  Multiplexer #(.select(4), .width(16)) multiplexer_1 (
    .in0(in_1), .in1({in_1[0], in_1[15:1]}), .in2({in_1[1:0], in_1[15:2]}), .in3({in_1[2:0], in_1[15:3]}),
    .in4({in_1[3:0], in_1[15:4]}), .in5({in_1[4:0], in_1[15:5]}), .in6({in_1[5:0], in_1[15:6]}),
    .in7({in_1[6:0], in_1[15:7]}), .in8({in_1[7:0], in_1[15:8]}), .in9({in_1[8:0], in_1[15:9]}),
    .in10({in_1[9:0], in_1[15:10]}), .in11({in_1[10:0], in_1[15:11]}), .in12({in_1[11:0], in_1[15:12]}),
    .in13({in_1[12:0], in_1[15:13]}), .in14({in_1[13:0], in_1[15:14]}), .in15({in_1[14:0], in_1[15]}),
    .out(out_3), .sel(in_2));  // open: en
endmodule
