// Logisim project cpu-pipelined.circ as structural Verilog: 6 circuits, main circuit main
module main (
  input  [15:0] INSTRUCTION,
  input  CLOCK,
  output [15:0] FETCH_ADDRESS,
  output [15:0] s0_Value,
  output [15:0] s1_Value,
  output [15:0] s2_Value,
  output [15:0] ra_Value,
  output [15:0] sp_Value,
  output [15:0] HI_Value,
  output [15:0] LO_Value
);

  wire ALUSrc, branch, Control_beq, Control_bne, Control_jr, ExtOp, flushPipeline, i_type_instr, j, jumping,
       load_store, lui, main_2_equal, MemToReg, MemWrite, mfhi, mfhi_en, mflo, mflo_en, not_1_out, RegWrite,
       u_type;
  wire [2:0] ALU_CTRL, extended_u_type_rd, multiplexer_1_out, multiplexer_2_out;
  wire [5:0] i_type_immediate;
  wire [15:0] adder_1_out, adder_2_out, bit_extender_2_out, bit_extender_3_out, bit_extender_4_out,
       main_1_read_data_1, main_1_read_data_2, main_2_result, main_2_result_2, MEM_p1, MEM_p6,
       multiplexer_3_out, multiplexer_4_out, multiplexer_5_out, multiplexer_6_out, multiplexer_7_out,
       multiplexer_8_out, multiplexer_10_out, multiplexer_11_out, shifter_1_out;
  wire [15:6] newInstruction;

  control Control (
    .INSTRUCTION({newInstruction, i_type_immediate}), .ExtOp(ExtOp), .alu_equals_output(main_2_equal),
    .u_type_instr(u_type), .j(j), .jr(Control_jr), .bne(Control_bne), .beq(Control_beq), .lui(lui),
    .MemToReg(MemToReg), .MemWrite(MemWrite), .load_store(load_store), .mflo_out(mflo_en),
    .mfhi_out(mfhi_en), .ALU_Control(ALU_CTRL), .RegWrite(RegWrite), .branching(branch),
    .i_type_instr(i_type_instr), .ALUSrc(ALUSrc), .mfhi(mfhi), .mflo(mflo), .jumping(jumping));
  assign extended_u_type_rd = {{1{1'b0}}, newInstruction[11:10]};  // Bit_Extender bit_extender_1
  Multiplexer #(.width(3), .enable("false")) multiplexer_1 (
    .in0(newInstruction[11:9]), .in1(extended_u_type_rd), .out(multiplexer_1_out), .sel(u_type));
  Multiplexer #(.width(3), .enable("false")) multiplexer_2 (
    .in0(i_type_immediate[5:3]), .in1(newInstruction[11:9]), .out(multiplexer_2_out), .sel(i_type_instr));
  assign bit_extender_2_out = {{10{1'b0}}, i_type_immediate};  // Bit_Extender bit_extender_2
  assign bit_extender_3_out = {{10{i_type_immediate[5]}}, i_type_immediate};  // Bit_Extender bit_extender_3
  regfile_main main_1 (
    .Read_Register_1(newInstruction[8:6]), .Read_Register_2(multiplexer_2_out),
    .Write_Register(multiplexer_1_out), .Write_Data(multiplexer_5_out), .Write_Enable(RegWrite),
    .Clock(CLOCK), .Read_Data_1(main_1_read_data_1), .Read_Data_2(main_1_read_data_2), .s0_Value(s0_Value),
    .s1_Value(s1_Value), .s2_Value(s2_Value), .ra_Value(ra_Value), .sp_Value(sp_Value));
  Multiplexer #(.width(16), .enable("false")) multiplexer_3 (
    .in0(bit_extender_2_out), .in1(bit_extender_3_out), .out(multiplexer_3_out), .sel(ExtOp));
  instruction_fetch instruction_fetch_1 (
    .i_type(i_type_immediate), .rs(main_1_read_data_1), .u_type({newInstruction[9:6], i_type_immediate}),
    .jr(Control_jr), .beq(Control_beq), .j_2(j), .zero(main_2_equal), .j(j), .bne(Control_bne),
    .clock(CLOCK), .fetched_instruction(FETCH_ADDRESS));  // open: rd
  Multiplexer #(.width(16), .enable("false")) multiplexer_4 (
    .in0(main_1_read_data_2), .in1(multiplexer_3_out), .out(multiplexer_4_out), .sel(ALUSrc));
  assign bit_extender_4_out = {{6{1'b0}}, {newInstruction[9:6], i_type_immediate}};  // Bit_Extender bit_extender_4
  alu_main main_2 (
    .Switch(ALU_CTRL), .X(main_1_read_data_1), .Equal(main_2_equal), .Result(main_2_result),
    .Y(multiplexer_4_out), .Result_2(main_2_result_2));
  not not_1 (not_1_out, j);
  Multiplexer #(.width(16), .enable("false")) multiplexer_5 (
    .in0(adder_2_out), .in1(multiplexer_10_out), .out(multiplexer_5_out), .sel(not_1_out));
  Shifter #(.width(16)) shifter_1 (.in(bit_extender_4_out), .\dist (4'b0110), .out(shifter_1_out));
  // mem_main MEM: pin names not known; wires that end beside it: MEM_p1, main_1_read_data_2, MemWrite, 4'b0110, CLOCK, MEM_p6, mflo
  Adder #(.width(16)) adder_1 (.a(main_1_read_data_1), .b(bit_extender_3_out), .out(adder_1_out));  // open: cin, cout
  Multiplexer #(.width(16), .enable("false")) multiplexer_6 (
    .in0(main_2_result), .in1(shifter_1_out), .out(multiplexer_6_out), .sel(lui));
  Register #(.width(16)) LO (.D(multiplexer_6_out), .en(mflo_en), .Q(LO_Value), .clk(CLOCK));  // open: clr
  Multiplexer #(.width(16), .enable("false")) multiplexer_7 (
    .in0(multiplexer_8_out), .in1(LO_Value), .out(multiplexer_7_out), .sel(mflo));
  Multiplexer #(.width(16), .enable("false")) multiplexer_8 (
    .in0(main_2_result), .in1(MEM_p6), .out(multiplexer_8_out), .sel(MemToReg));
  Multiplexer #(.width(16), .enable("false")) multiplexer_9 (
    .in0(main_2_result), .in1(adder_1_out), .out(MEM_p1), .sel(load_store));
  Adder #(.width(16)) adder_2 (.a(FETCH_ADDRESS), .b({16{1'b0}}), .out(adder_2_out));  // open: cin, cout
  Register #(.width(16)) HI (.D(main_2_result_2), .en(mfhi_en), .Q(HI_Value), .clk(CLOCK));  // open: clr
  Multiplexer #(.width(16), .enable("false")) multiplexer_10 (
    .in0(multiplexer_7_out), .in1(HI_Value), .out(multiplexer_10_out), .sel(mfhi));
  or or_1 (flushPipeline, jumping, branch);
  Multiplexer #(.width(16), .enable("false")) multiplexer_11 (
    .in0(INSTRUCTION), .in1({16{1'b0}}), .out(multiplexer_11_out), .sel(flushPipeline));
  Register #(.width(16)) register_1 (
    .D(multiplexer_11_out), .Q({newInstruction, i_type_immediate}), .clk(CLOCK));  // open: en, clr

  // Other names for the same wires on the sheet: clk = CLOCK; fetch_addr[15:0] = FETCH_ADDRESS; hi[15:0] = HI_Value;
  //   lo[15:0] = LO_Value; newInstruction[5:0] = i_type_immediate;
  //   u_type_immediate[9:0] = {newInstruction[9:6], i_type_immediate}; u_type_rd[1:0] = newInstruction[11:10];
  //   ra[15:0] = ra_Value; s0[15:0] = s0_Value; s1[15:0] = s1_Value; s2[15:0] = s2_Value; sp[15:0] = sp_Value

  // Notes on the sheet:
  //   Output
  //   These are outputs/inputs from run.circ
  //   Inputs
  //   These are DEBUG/TEST outputs from your circuit.
endmodule

module control (
  input  [15:0] INSTRUCTION,
  input  alu_equals_output,
  output j,
  output jr,
  output bne,
  output beq,
  output ExtOp,
  output lui,
  output MemToReg,
  output MemWrite,
  output load_store,
  output mflo_out,
  output mfhi_out,
  output [2:0] ALU_Control,
  output RegWrite,
  output branching,
  output i_type_instr,
  output ALUSrc,
  output mfhi,
  output mflo,
  output u_type_instr,
  output jumping
);

  wire addi, and_4_out, and_5_out, and_16_out, and_17_out, and_18_out, and_19_out, and_20_out, and_21_out,
       and_22_out, and_23_out, and_24_out, and_25_out, and_26_out, and_27_out, and_28_out, and_30_out,
       and_31_out, and_32_out, and_33_out, and_34_out, and_35_out, and_36_out, and_37_out, and_38_out,
       and_39_out, and_40_out, and_41_out, and_42_out, and_43_out, and_44_out, and_45_out, and_46_out,
       and_47_out, and_48_out, and_49_out, and_50_out, and_51_out, and_52_out, and_53_out, and_54_out,
       and_55_out, and_56_out, and_57_out, and_58_out, and_59_out, and_60_out, and_61_out, and_62_out,
       and_63_out, and_64_out, and_65_out, and_66_out, and_67_out, and_68_out, and_69_out, and_70_out,
       and_71_out, and_72_out, and_73_out, and_74_out, and_75_out, and_76_out, and_77_out, and_78_out,
       and_79_out, and_80_out, and_81_out, and_82_out, and_83_out, and_84_out, and_85_out, and_86_out,
       and_87_out, and_88_out, and_89_out, and_90_out, and_91_out, and_92_out, and_93_out, and_94_out,
       and_95_out, and_96_out, and_97_out, and_98_out, and_99_out, and_100_out, and_101_out, and_102_out,
       and_103_out, andi, lh, lui_t, mult, multiplexer_1_out, ori, R_Type, sh, slti;
  wire [2:0] addi_extend, and_2_out, and_3_out, and_6_out, and_7_out, and_8_out, and_9_out, and_10_out,
       and_11_out, and_12_out, and_13_out, and_14_out, and_15_out, andi_extend, beq_extend, bne_extend,
       j_extend, jr_extend, lh_extend, lui_extend, ori_extend, R_Extend, sh_extend, slti_extend;

  assign R_Extend = {{2{R_Type}}, R_Type};  // Bit_Extender bit_extender_1
  assign addi_extend = {{2{addi}}, addi};  // Bit_Extender bit_extender_2
  assign slti_extend = {{2{slti}}, slti};  // Bit_Extender bit_extender_3
  assign andi_extend = {{2{andi}}, andi};  // Bit_Extender bit_extender_4
  assign ori_extend = {{2{ori}}, ori};  // Bit_Extender bit_extender_5
  assign lui_extend = {{2{lui_t}}, lui_t};  // Bit_Extender bit_extender_6
  assign j_extend = {{2{j}}, j};  // Bit_Extender bit_extender_7
  assign jr_extend = {{2{jr}}, jr};  // Bit_Extender bit_extender_8
  assign beq_extend = {{2{beq}}, beq};  // Bit_Extender bit_extender_9
  assign bne_extend = {{2{bne}}, bne};  // Bit_Extender bit_extender_10
  assign lh_extend = {{2{lh}}, lh};  // Bit_Extender bit_extender_11
  assign sh_extend = {{2{sh}}, sh};  // Bit_Extender bit_extender_12
  and and_1 (lui, lui_t, 1'b1);
  decode_instruction decode_instruction_1 (
    .opcode(INSTRUCTION[15:12]), .R_Type(R_Type), .lui(lui_t), .jump(j), .jump_register(jr), .beq(beq),
    .bne(bne), .addi(addi), .slti(slti), .andi(andi), .ori(ori), .load_halfword(lh), .store_halfword(sh),
    .move_from_hi(mfhi), .move_from_lo(mflo));
  r_decode r_decode_1 (
    .opcode(INSTRUCTION[15:12]), .in_2(INSTRUCTION[2:0]), .mult(mult));  // open: sll, srl, add, and, or, xor, slt
  assign and_2_out = 3'b011 & andi_extend;  // AND_Gate and_2, 3 bits wide
  assign and_3_out = 3'b100 & ori_extend;  // AND_Gate and_3, 3 bits wide
  and and_4 (and_4_out, lui_t, 1'b1);
  and and_5 (and_5_out, mult, 1'b1);
  assign and_6_out = INSTRUCTION[2:0] & R_Extend;  // AND_Gate and_6, 3 bits wide
  assign and_7_out = 3'b000 & lui_extend;  // AND_Gate and_7, 3 bits wide
  assign and_8_out = 3'b010 & j_extend;  // AND_Gate and_8, 3 bits wide
  assign and_9_out = 3'b010 & jr_extend;  // AND_Gate and_9, 3 bits wide
  assign and_10_out = 3'b010 & beq_extend;  // AND_Gate and_10, 3 bits wide
  assign and_11_out = 3'b010 & bne_extend;  // AND_Gate and_11, 3 bits wide
  assign and_12_out = 3'b010 & lh_extend;  // AND_Gate and_12, 3 bits wide
  assign and_13_out = 3'b010 & sh_extend;  // AND_Gate and_13, 3 bits wide
  assign and_14_out = 3'b010 & addi_extend;  // AND_Gate and_14, 3 bits wide
  assign and_15_out = 3'b110 & slti_extend;  // AND_Gate and_15, 3 bits wide
  or or_1 (mflo_out, and_4_out, and_5_out);
  and and_16 (and_16_out, ori, 1'b0);
  assign ALU_Control = and_6_out | and_7_out | and_8_out | and_9_out | and_10_out | and_11_out | and_12_out | and_13_out | and_14_out | and_15_out | and_2_out | and_3_out;  // OR_Gate or_2, 3 bits wide
  and and_17 (and_17_out, slti, 1'b1);
  and and_18 (and_18_out, ori, 1'b1);
  and and_19 (and_19_out, lh, 1'b1);
  and and_20 (and_20_out, sh, 1'b1);
  and and_21 (and_21_out, jr, 1'b1);
  and and_22 (and_22_out, beq, 1'b1);
  and and_23 (and_23_out, bne, 1'b1);
  and and_24 (and_24_out, addi, 1'b1);
  and and_25 (and_25_out, slti, 1'b1);
  and and_26 (and_26_out, lh, 1'b1);
  and and_27 (and_27_out, sh, 1'b1);
  and and_28 (and_28_out, andi, 1'b0);
  and and_29 (mfhi_out, mult, 1'b1);
  and and_30 (and_30_out, R_Type, 1'b0);
  and and_31 (and_31_out, lui_t, 1'b0);
  and and_32 (and_32_out, beq, 1'b0);
  and and_33 (and_33_out, bne, 1'b0);
  and and_34 (and_34_out, addi, 1'b1);
  and and_35 (and_35_out, andi, 1'b1);
  or or_3 (ExtOp, and_21_out, and_22_out, and_23_out, and_24_out, and_25_out, and_26_out, and_27_out, and_28_out, and_16_out);
  or or_4 (ALUSrc, and_30_out, and_31_out, and_32_out, and_33_out, and_34_out, and_17_out, and_35_out, and_18_out, and_19_out, and_20_out);
  and and_36 (and_36_out, ori, 1'b0);
  and and_37 (and_37_out, lh, 1'b0);
  and and_38 (and_38_out, sh, 1'b1);
  and and_39 (and_39_out, mfhi, 1'b0);
  and and_40 (and_40_out, mflo, 1'b0);
  and and_41 (and_41_out, lui_t, 1'b1);
  and and_42 (and_42_out, j, 1'b1);
  and and_43 (and_43_out, jr, 1'b1);
  and and_44 (and_44_out, R_Type, 1'b0);
  and and_45 (and_45_out, lui_t, 1'b0);
  and and_46 (and_46_out, addi, 1'b0);
  and and_47 (and_47_out, slti, 1'b0);
  and and_48 (and_48_out, andi, 1'b0);
  and and_49 (and_49_out, R_Type, 1'b1);
  and and_50 (and_50_out, beq, 1'b0);
  and and_51 (and_51_out, bne, 1'b0);
  and and_52 (and_52_out, addi, 1'b1);
  and and_53 (and_53_out, slti, 1'b1);
  and and_54 (and_54_out, andi, 1'b1);
  and and_55 (and_55_out, ori, 1'b1);
  and and_56 (and_56_out, lh, 1'b1);
  and and_57 (and_57_out, sh, 1'b0);
  and and_58 (and_58_out, mfhi, 1'b1);
  or or_5 (MemWrite, and_44_out, and_45_out, and_46_out, and_47_out, and_48_out, and_36_out, and_37_out, and_38_out, and_39_out, and_40_out);
  and and_59 (and_59_out, mflo, 1'b1);
  or or_6 (RegWrite, and_59_out, and_49_out, and_41_out, and_42_out, and_43_out, and_50_out, and_51_out, and_52_out, and_53_out, and_54_out, and_55_out, and_56_out, and_57_out, and_58_out);
  and and_60 (and_60_out, R_Type, 1'b0);
  and and_61 (and_61_out, lh, 1'b1);
  and and_62 (and_62_out, sh, 1'b1);
  and and_63 (and_63_out, beq, 1'b1);
  and and_64 (and_64_out, lh, 1'b1);
  and and_65 (and_65_out, sh, 1'b1);
  and and_66 (and_66_out, addi, 1'b1);
  and and_67 (and_67_out, slti, 1'b1);
  and and_68 (and_68_out, andi, 1'b1);
  and and_69 (and_69_out, ori, 1'b1);
  and and_70 (and_70_out, bne, 1'b1);
  and and_71 (and_71_out, R_Type, 1'b0);
  and and_72 (and_72_out, j, 1'b1);
  and and_73 (and_73_out, jr, 1'b1);
  and and_74 (and_74_out, R_Type, 1'b0);
  or or_7 (jumping, and_71_out, and_72_out, and_73_out);
  or or_8 (load_store, and_60_out, and_61_out, and_62_out);
  or or_9 (i_type_instr, and_76_out, and_63_out, and_74_out, and_64_out, and_65_out, and_66_out, and_67_out, and_68_out, and_69_out, and_70_out, and_75_out);
  and and_75 (and_75_out, mflo, 1'b1);
  and and_76 (and_76_out, mfhi, 1'b1);
  and and_77 (and_77_out, bne, 1'b1);
  and and_78 (and_78_out, R_Type, 1'b0);
  and and_79 (and_79_out, lui_t, 1'b0);
  and and_80 (and_80_out, j, 1'b0);
  and and_81 (and_81_out, jr, 1'b0);
  and and_82 (and_82_out, beq, 1'b0);
  and and_83 (and_83_out, bne, 1'b0);
  and and_84 (and_84_out, addi, 1'b0);
  and and_85 (and_85_out, slti, 1'b0);
  and and_86 (and_86_out, andi, 1'b0);
  and and_87 (and_87_out, ori, 1'b0);
  and and_88 (and_88_out, lh, 1'b1);
  and and_89 (and_89_out, sh, 1'b0);
  and and_90 (and_90_out, beq, 1'b1);
  and and_91 (and_91_out, R_Type, 1'b0);
  and and_92 (and_92_out, lui_t, 1'b1);
  and and_93 (and_93_out, j, 1'b1);
  and and_94 (and_94_out, jr, 1'b0);
  and and_95 (and_95_out, beq, 1'b0);
  and and_96 (and_96_out, bne, 1'b0);
  and and_97 (and_97_out, addi, 1'b0);
  and and_98 (and_98_out, slti, 1'b0);
  and and_99 (and_99_out, andi, 1'b0);
  and and_100 (and_100_out, ori, 1'b0);
  and and_101 (and_101_out, lh, 1'b0);
  and and_102 (and_102_out, sh, 1'b0);
  and and_103 (and_103_out, R_Type, 1'b0);
  or or_10 (MemToReg, and_78_out, and_79_out, and_80_out, and_81_out, and_82_out, and_83_out, and_84_out, and_85_out, and_86_out, and_87_out, and_88_out, and_89_out);
  or or_11 (branching, and_103_out, multiplexer_1_out);
  Multiplexer multiplexer_1 (
    .in0(and_77_out), .in1(and_90_out), .out(multiplexer_1_out), .sel(alu_equals_output));  // open: en
  or or_12 (u_type_instr, and_91_out, and_92_out, and_93_out, and_94_out, and_95_out, and_96_out, and_97_out, and_98_out, and_99_out, and_100_out, and_101_out, and_102_out);

  // Other names for the same wires on the sheet: funct[2:0] = INSTRUCTION[2:0]; rt[2:0] = INSTRUCTION[5:3];
  //   rs[2:0] = INSTRUCTION[8:6]; rd[2:0] = INSTRUCTION[11:9]; opcode[3:0] = INSTRUCTION[15:12]

  // Notes on the sheet:
  //   R-Type Instruction
endmodule

module decode_instruction (
  input  [3:0] opcode,
  output R_Type,
  output lui,
  output jump,
  output jump_register,
  output beq,
  output bne,
  output addi,
  output slti,
  output andi,
  output ori,
  output load_halfword,
  output store_halfword,
  output move_from_hi,
  output move_from_lo
);

  Decoder #(.select(4), .enable("false")) decoder_1 (
    .out0(R_Type), .out1(lui), .out2(jump), .out3(jump_register), .out4(beq), .out5(bne), .out6(addi),
    .out7(slti), .out8(andi), .out9(ori), .out10(load_halfword), .out11(store_halfword),
    .out12(move_from_hi), .out13(move_from_lo), .sel(opcode));  // open: out14, out15

  // Notes on the sheet:
  //   opcode
endmodule

module instruction_fetch (
  input  jr,
  input  beq,
  input  zero,
  input  bne,
  input  j,
  input  clock,
  input  j_2,
  input  [5:0] i_type,
  input  [15:0] rs,
  input  [9:0] u_type,
  output [15:0] rd,
  output [15:0] fetched_instruction
);

  wire and_1_out, and_2_out, not_1_out, or_1_out;
  wire [9:0] address;
  wire [15:0] adder_2_out, bit_extender_1_out, bit_extender_2_out, imm___rs, multiplexer_1_out,
       multiplexer_2_out, multiplexer_4_out, multiplexer_5_out, subtractor_1_out;
  wire [15:10] immediate;

  and and_1 (and_1_out, beq, zero);
  Adder #(.width(16)) adder_1 (.a(16'h2), .b(fetched_instruction), .out(rd));  // open: cin, cout
  assign bit_extender_1_out = {{10{i_type[5]}}, i_type};  // Bit_Extender bit_extender_1
  assign bit_extender_2_out = {{6{u_type[9]}}, u_type};  // Bit_Extender bit_extender_2
  not not_1 (not_1_out, zero);
  or or_1 (or_1_out, and_1_out, and_2_out);
  Multiplexer #(.width(16), .enable("false")) multiplexer_1 (
    .in0(rd), .in1(imm___rs), .out(multiplexer_1_out), .sel(jr));
  Multiplexer #(.width(16), .enable("false")) multiplexer_2 (
    .in0(multiplexer_1_out), .in1(adder_2_out), .out(multiplexer_2_out), .sel(or_1_out));
  Multiplexer #(.width(16), .enable("false")) multiplexer_3 (
    .in0(bit_extender_1_out), .in1(bit_extender_2_out), .out({immediate, address}), .sel(j_2));
  and and_2 (and_2_out, not_1_out, bne);
  Multiplexer #(.width(16), .enable("false")) multiplexer_4 (
    .in0(multiplexer_2_out), .in1({fetched_instruction[15:10], address}), .out(multiplexer_4_out), .sel(j));
  Adder #(.width(16)) adder_2 (
    .a(fetched_instruction), .b({immediate, address}), .out(adder_2_out));  // open: cin, cout
  Adder #(.width(16)) adder_3 (.a({immediate, address}), .b(rs), .out(imm___rs));  // open: cin, cout
  Multiplexer #(.width(16)) multiplexer_5 (
    .in0(multiplexer_4_out), .in1(subtractor_1_out), .out(multiplexer_5_out), .sel(or_1_out));  // open: en
  Subtractor #(.width(16)) subtractor_1 (.a(multiplexer_4_out), .b(16'h2), .out(subtractor_1_out));  // open: bin, bout
  Register #(.width(16)) register_1 (.D(multiplexer_5_out), .Q(fetched_instruction), .clk(clock));  // open: en, clr

  // Other names for the same wires on the sheet: immediate[9:0] = address;
  //   address[15:10] = fetched_instruction[15:10]; PC[15:0] = fetched_instruction
endmodule

module r_decode (
  input  [3:0] opcode,
  input  [2:0] in_2,
  output sll,
  output srl,
  output add,
  output \and ,
  output \or ,
  output \xor ,
  output slt,
  output mult
);

  wire decode_instruction_1_r_type;
  wire [2:0] and_1_out, bit_extender_1_out;

  decode_instruction decode_instruction_1 (
    .opcode(opcode), .R_Type(decode_instruction_1_r_type));  // open: lui, jump, jump_register, beq, bne, addi, slti, andi, ori, load_halfword, store_halfword, move_from_hi, move_from_lo
  assign bit_extender_1_out = {{2{decode_instruction_1_r_type}}, decode_instruction_1_r_type};  // Bit_Extender bit_extender_1
  assign and_1_out = bit_extender_1_out & in_2;  // AND_Gate and_1, 3 bits wide
  Decoder #(.select(3), .enable("false")) decoder_1 (
    .out0(sll), .out1(srl), .out2(add), .out3(\and ), .out4(\or ), .out5(\xor ), .out6(slt), .out7(mult),
    .sel(and_1_out));
endmodule

module fetch (
  input  j,
  input  jr,
  input  bne,
  input  beq,
  input  zero,
  input  [9:0] immediate_u,
  input  [5:0] immediate_i,
  input  [15:0] rd,
  input  clk,
  output [15:0] fetched_instruction
);

  wire and_1_out, and_2_out, not_1_out, or_1_out;
  wire [15:0] adder_1_out, adder_2_out, multiplexer_2_out, multiplexer_3_out, undriven;

  Adder #(.width(16)) adder_1 (.a(16'h2), .b(fetched_instruction), .out(adder_1_out));  // open: cin, cout
  not not_1 (not_1_out, zero);
  and and_1 (and_1_out, beq, zero);
  Multiplexer #(.width(16), .enable("false")) multiplexer_1 (
    .in0({fetched_instruction[15:10], immediate_u}), .in1({fetched_instruction[15:6], immediate_i}), .sel(j));  // open: out
  and and_2 (and_2_out, bne, not_1_out);
  or or_1 (or_1_out, and_1_out, and_2_out, jr);
  Multiplexer #(.width(16), .enable("false")) multiplexer_2 (
    .in0(adder_1_out), .in1(undriven), .out(multiplexer_2_out), .sel(or_1_out));
  Multiplexer #(.width(16), .enable("false")) multiplexer_3 (
    .in0(multiplexer_2_out), .in1(adder_2_out), .out(multiplexer_3_out), .sel(j));
  Adder #(.width(16)) adder_2 (.a(16'h2), .b(rd), .out(adder_2_out));  // open: cin, cout
  Register #(.width(16)) pc (.D(multiplexer_3_out), .Q(fetched_instruction), .clk(clk));  // open: en, clr
endmodule
