// Logisim project regfile.circ as structural Verilog: 1 circuit, main circuit main
module main (
  input  [2:0] Read_Register_1,
  input  [2:0] Read_Register_2,
  input  [2:0] Write_Register,
  input  [15:0] Write_Data,
  input  Write_Enable,
  input  Clock,
  output [15:0] s0_Value,
  output [15:0] s1_Value,
  output [15:0] s2_Value,
  output [15:0] ra_Value,
  output [15:0] sp_Value,
  output [15:0] Read_Data_1,
  output [15:0] Read_Data_2
);

  wire regOutput1, regOutput2, regOutput3, regOutput4, regOutput5, regOutput6, regOutput7;
  wire [15:0] a0_1_2_output, a0_1_output, s0_1_2output, v0_1_2_output, v0_1_output;

  Demultiplexer #(.select(3), .enable("false")) demultiplexer_1 (
    .out1(regOutput1), .out2(regOutput2), .out3(regOutput3), .out4(regOutput4), .out5(regOutput5),
    .out6(regOutput6), .out7(regOutput7), .in(Write_Enable), .sel(Write_Register));  // open: out0
  Multiplexer #(.select(3), .width(16)) multiplexer_1 (
    .in0({16{1'b0}}), .in1(ra_Value), .in2(s0_Value), .in3(s1_Value), .in4(s2_Value), .in5(a0_1_output),
    .in6(v0_1_output), .in7(sp_Value), .out(Read_Data_1), .sel(Read_Register_1));  // open: en
  Register #(.width(16)) ra_1 (.D(Write_Data), .en(regOutput1), .Q(ra_Value), .clk(Clock));  // open: clr
  Register #(.width(16)) s0_1 (.D(Write_Data), .en(regOutput2), .Q(s0_Value), .clk(Clock));  // open: clr
  Register #(.width(16)) s1_1 (.D(Write_Data), .en(regOutput3), .Q(s1_Value), .clk(Clock));  // open: clr
  Register #(.width(16)) s2_1 (.D(Write_Data), .en(regOutput4), .Q(s2_Value), .clk(Clock));  // open: clr
  Register #(.width(16)) a0_1 (.D(Write_Data), .en(regOutput5), .Q(a0_1_output), .clk(Clock));  // open: clr
  Register #(.width(16)) v0_1 (.D(Write_Data), .en(regOutput6), .Q(v0_1_output), .clk(Clock));  // open: clr
  Register #(.width(16)) sp_1 (.D(Write_Data), .en(regOutput7), .Q(sp_Value), .clk(Clock));  // open: clr
  Multiplexer #(.select(3), .width(16)) multiplexer_2 (
    .in0({16{1'b0}}), .in1(ra_Value), .in2(s0_Value), .in3(s1_Value), .in4(s2_Value), .in5(a0_1_2_output),
    .in6(v0_1_2_output), .in7(sp_Value), .out(Read_Data_2), .sel(Read_Register_2));  // open: en
  Register #(.width(16)) ra_2 (.D(Write_Data), .en(regOutput1), .Q(ra_Value), .clk(Clock));  // open: clr
  Register #(.width(16)) s0_2 (.D(Write_Data), .en(regOutput2), .Q(s0_1_2output), .clk(Clock));  // open: clr
  Register #(.width(16)) s1_2 (.D(Write_Data), .en(regOutput3), .Q(s1_Value), .clk(Clock));  // open: clr
  Register #(.width(16)) s2_2 (.D(Write_Data), .en(regOutput4), .Q(s2_Value), .clk(Clock));  // open: clr
  Register #(.width(16)) a0_1_2 (.D(Write_Data), .en(regOutput5), .Q(a0_1_2_output), .clk(Clock));  // open: clr
  Register #(.width(16)) v0_2 (.D(Write_Data), .en(regOutput6), .Q(v0_1_2_output), .clk(Clock));  // open: clr
  Register #(.width(16)) sp_2 (.D(Write_Data), .en(regOutput7), .Q(sp_Value), .clk(Clock));  // open: clr

  // Other names for the same wires on the sheet: clk = Clock; Clock_1 = Clock; Clock_1_2 = Clock; Clock_2 = Clock;
  //   Clock_2_2 = Clock; Clock_3 = Clock; Clock_3_2 = Clock; Clock_4 = Clock; Clock_4_2 = Clock; Clock_5 = Clock;
  //   Clock_5_2 = Clock; Clock_6 = Clock; Clock_6_2 = Clock; Clock_7 = Clock; Clock_7_2 = Clock;
  //   ra_1_2_output[15:0] = ra_Value; ra_1_output[15:0] = ra_Value; read_data1[15:0] = Read_Data_1;
  //   read_data2[15:0] = Read_Data_2; read_reg1[2:0] = Read_Register_1; read_reg2[2:0] = Read_Register_2;
  //   regOutput1_2 = regOutput1; regOutput2_2 = regOutput2; regOutput3_2 = regOutput3; regOutput4_2 = regOutput4;
  //   regOutput5_2 = regOutput5; regOutput6_2 = regOutput6; regOutput7_2 = regOutput7; s0_1_2_output[15:0] = s0_Value;
  //   s0_1_output[15:0] = s0_Value; s1_1_2_output[15:0] = s1_Value; s1_1_output[15:0] = s1_Value;
  //   s2_1_2_output[15:0] = s2_Value; s2_1_output[15:0] = s2_Value; sp_1_2_output[15:0] = sp_Value;
  //   sp_1_output[15:0] = sp_Value; write_data_1[15:0] = Write_Data; write_data_1_2[15:0] = Write_Data;
  //   write_data_2[15:0] = Write_Data; write_data_2_2[15:0] = Write_Data; write_data_3[15:0] = Write_Data;
  //   write_data_3_2[15:0] = Write_Data; write_data_4[15:0] = Write_Data; write_data_4_2[15:0] = Write_Data;
  //   write_data_5[15:0] = Write_Data; write_data_5_2[15:0] = Write_Data; write_data_6[15:0] = Write_Data;
  //   write_data_6_2[15:0] = Write_Data; write_data_7[15:0] = Write_Data; write_data_7_2[15:0] = Write_Data;
  //   write_en = Write_Enable; write_reg[2:0] = Write_Register

  // Notes on the sheet:
  //   INPUTS to your circuit
  //   DON'T CHANGE THE LOCATIONS OF THE INPUTS AND OUTPUTS!
  //   These are DEBUG/TEST outputs from your circuit.
  //   OUTPUTS from your circuit
endmodule
