// Logisim project alu.circ as structural Verilog: 1 circuit, main circuit main
module main (
  input  [15:0] X,
  input  [15:0] Y,
  input  [2:0] Switch,
  output Equal,
  output [15:0] Result,
  output [15:0] Result_2
);

  wire comparator_1_lt;
  wire [3:0] bit_extender_1_out, bit_extender_2_out;
  wire [15:0] add, \and , mlo, \or , sll, slt, srl, \xor ;

  Multiplexer #(.select(3), .width(16)) multiplexer_1 (
    .in0(sll), .in1(srl), .in2(add), .in3(\and ), .in4(\or ), .in5(\xor ), .in6(slt), .in7(mlo),
    .out(Result), .sel(Switch));  // open: en
  Bit_Extender #(.in_width(16), .out_width(4)) bit_extender_1 (.in(Y), .out(bit_extender_1_out));
  Shifter #(.width(16), .shift("lr")) shifter_1 (.in(X), .\dist (bit_extender_2_out), .out(srl));
  Bit_Extender #(.in_width(16), .out_width(4)) bit_extender_2 (.in(Y), .out(bit_extender_2_out));
  Adder #(.width(16)) adder_1 (.a(X), .b(Y), .out(add));  // open: cin, cout
  assign \and  = X & Y;  // AND_Gate and_1, 16 bits wide
  assign \or  = X | Y;  // OR_Gate or_1, 16 bits wide
  assign \xor  = X ^ Y;  // XOR_Gate xor_1, 16 bits wide
  Shifter #(.width(16)) shifter_2 (.in(X), .\dist (bit_extender_1_out), .out(sll));
  Comparator #(.width(16)) comparator_1 (.a(X), .b(Y), .eq(Equal), .lt(comparator_1_lt));  // open: gt
  Multiplier #(.width(16)) multiplier_1 (.a(X), .b(Y), .out(mlo), .cout(Result_2));  // open: cin
  assign slt = {{15{1'b0}}, comparator_1_lt};  // Bit_Extender bit_extender_3

  // Other names for the same wires on the sheet: S[2:0] = Switch; add_input1[15:0] = X; and_input1[15:0] = X;
  //   mult_input1[15:0] = X; or_input1[15:0] = X; sll_input1[15:0] = X; slteq_input1[15:0] = X; srl_input1[15:0] = X;
  //   xor_input1[15:0] = X; add_input2[15:0] = Y; and_input2[15:0] = Y; mult_input2[15:0] = Y; or_input2[15:0] = Y;
  //   sll_input2[15:0] = Y; slteq_input2[15:0] = Y; srl_input2[15:0] = Y; xor_input2[15:0] = Y

  // Notes on the sheet:
  //   INPUTS to your circuit
  //   DON'T CHANGE THE LOCATIONS OF THE INPUTS AND OUTPUTS!
  //   OUTPUTS from your circuit
endmodule
